// Logisim project full adder.circ as structural Verilog: 1 circuit, main circuit main
module main (
  input  in_1,
  input  in_2,
  input  in_3,
  input  in_4,
  input  in_5,
  input  in_6,
  input  in_7,
  input  in_8,
  input  in_9,
  input  in_10,
  input  in_11,
  input  in_12,
  output out_13,
  output out_14,
  output out_15,
  output out_16,
  output out_17,
  output out_18,
  output out_19,
  output out_20
);

  wire and_1_out, and_2_out, and_3_out, and_4_out, and_5_out, and_6_out, and_7_out, and_8_out, xor_1_out,
       xor_2_out, xor_3_out, xor_7_out;

  xor xor_1 (xor_1_out, in_10, in_11);
  and and_1 (and_1_out, in_10, in_11);
  xor xor_2 (xor_2_out, in_1, in_2);
  and and_2 (and_2_out, in_1, in_2);
  xor xor_3 (xor_3_out, in_4, in_6);
  and and_3 (and_3_out, in_4, in_6);
  xor xor_4 (out_19, xor_1_out, in_12);
  and and_4 (and_4_out, xor_1_out, in_12);
  xor xor_5 (out_13, xor_2_out, in_3);
  and and_5 (and_5_out, xor_2_out, in_3);
  xor xor_6 (out_15, xor_3_out, in_8);
  and and_6 (and_6_out, xor_3_out, in_8);
  or or_1 (out_20, and_4_out, and_1_out);
  or or_2 (out_14, and_5_out, and_2_out);
  or or_3 (out_17, and_6_out, and_3_out);
  xor xor_7 (xor_7_out, in_5, in_7);
  and and_7 (and_7_out, in_5, in_7);
  xor xor_8 (out_16, xor_7_out, in_9);
  and and_8 (and_8_out, xor_7_out, in_9);
  or or_4 (out_18, and_8_out, and_7_out);
endmodule
