// Logisim project full subtractor.circ as structural Verilog: 1 circuit, main circuit main
module main (
  input  in_1,
  input  in_2,
  input  in_3,
  input  in_4,
  input  in_5,
  output out_6,
  output out_7,
  output out_8,
  output out_9,
  output out_10,
  output out_11,
  output out_12,
  output out_13
);

  wire and_1_out, and_2_out, and_3_out, and_4_out, and_5_out, and_6_out, and_7_out, and_8_out, not_1_out,
       not_2_out, not_3_out, not_4_out, not_5_out, not_6_out, not_7_out, not_8_out, undriven, undriven_2,
       undriven_3, undriven_4, undriven_5, undriven_6, undriven_7, xnor_1_out, xnor_2_out, xnor_5_out,
       xnor_6_out;

  not not_1 (not_1_out, in_1);
  xnor xnor_1 (xnor_1_out, in_1, in_2);
  and and_1 (and_1_out, not_1_out, in_2);
  not not_2 (not_2_out, undriven);
  xnor xnor_2 (xnor_2_out, undriven, in_5);
  and and_2 (and_2_out, not_2_out, in_5);
  not not_3 (not_3_out, xnor_1_out);
  not not_4 (not_4_out, xnor_2_out);
  xnor xnor_3 (out_6, xnor_1_out, undriven_2);
  and and_3 (and_3_out, not_3_out, undriven_2);
  xnor xnor_4 (out_11, xnor_2_out, undriven_3);
  and and_4 (and_4_out, not_4_out, undriven_3);
  or or_1 (out_8, and_3_out, and_1_out);
  or or_2 (out_13, and_4_out, and_2_out);
  not not_5 (not_5_out, undriven_4);
  not not_6 (not_6_out, undriven_5);
  xnor xnor_5 (xnor_5_out, undriven_4, in_3);
  and and_5 (and_5_out, not_5_out, in_3);
  xnor xnor_6 (xnor_6_out, undriven_5, in_4);
  and and_6 (and_6_out, not_6_out, in_4);
  not not_7 (not_7_out, xnor_5_out);
  not not_8 (not_8_out, xnor_6_out);
  xnor xnor_7 (out_7, xnor_5_out, undriven_6);
  and and_7 (and_7_out, not_7_out, undriven_6);
  xnor xnor_8 (out_10, xnor_6_out, undriven_7);
  and and_8 (and_8_out, not_8_out, undriven_7);
endmodule
