// Logisim project half adder.circ as structural Verilog: 1 circuit, main circuit main
module main (
  input  in_1,
  input  in_2,
  input  in_3,
  input  in_4,
  input  in_5,
  input  in_6,
  input  in_7,
  input  in_8,
  output out_9,
  output out_10,
  output out_11,
  output out_12,
  output out_13,
  output out_14,
  output out_15,
  output out_16
);

  xor xor_1 (out_10, in_2, in_4);
  and and_1 (out_12, in_2, in_4);
  xor xor_2 (out_14, in_7, in_8);
  and and_2 (out_16, in_7, in_8);
  xor xor_3 (out_9, in_1, in_3);
  and and_3 (out_11, in_1, in_3);
  xor xor_4 (out_13, in_5, in_6);
  and and_4 (out_15, in_5, in_6);
endmodule
